# Fritzing sketch RCCar_BT (saved by Fritzing 0.9.3b)
breadboards: 2

parts:
  LED1 = smd LED [color="Red (633nm)" package="1206 [SMD]"]
  BAT2 = BC9VPC [package=bc9vpc]
  BAT1 = BC9VPC [package=bc9vpc]
  IC1 = L293D [package=THT]
  LED2 = smd LED [color="Red (633nm)" package="1206 [SMD]"]
  R2 = Resistor [tolerance=±5% resistance=330 package=THT]
  R1 = Resistor [tolerance=±5% resistance=330 package=THT]
  M2 = DC Motor
  M1 = DC Motor
  Part1 = Arduino Uno (Rev3)

nets:
  N1: LED1.cathode, BAT2.V-, BAT1.V-, IC1.0V, LED2.cathode, Part1.GND
  N2: LED1.anode, R2.Pin_0
  N3: BAT2.V+, Part1.5V
  N4: BAT1.V+, IC1.+Vmotor
  N5: IC1.Enable_1, Part1.D6_PWM
  N6: IC1.In_1, Part1.A5/SCL
  N7: IC1.Out_1_(_Controlled_by_Enable_1_), M1.pin_2
  N8: IC1.Out_2_(_Controlled_by_Enable_1_), M1.pin_1
  N9: IC1.In_2, Part1.A4/SDA
  N10: IC1.Enable_2, IC1.+V
  N11: IC1.In_3, Part1.A1
  N12: IC1.Out_3_(_Controlled_by_Enable_2_), M2.pin_1
  N13: IC1.Out_4_(_Controlled_by_Enable_2_), M2.pin_2
  N14: IC1.In_4, Part1.A0
  N15: LED2.anode, R1.Pin_0
  N16: R2.Pin_1, Part1.A3
  N17: R1.Pin_1, Part1.A2

notes:
  Wheel
  Motor
  Error
  Brown

// code stored in the sketch: Car.ino

/***************************************************
 Car Firmware - Oded Cnaan 2016
      
 ****************************************************/
#include <Adafruit_CC3000.h>
#include <SPI.h>
#include "utility/debug.h"
#include "utility/socket.h"

/****************** Wi-Fi Sheild ********************/
// These are the interrupt and control pins
#define ADAFRUIT_CC3000_IRQ   3  // MUST be an interrupt pin!
// These can be any two pins
#define ADAFRUIT_CC3000_VBAT  5
#define ADAFRUIT_CC3000_CS    10
// Use hardware SPI for the remaining pins
// On an UNO, SCK = 13, MISO = 12, and MOSI = 11
Adafruit_CC3000 cc3000 = Adafruit_CC3000(ADAFRUIT_CC3000_CS, ADAFRUIT_CC3000_IRQ, ADAFRUIT_CC3000_VBAT,
                                         SPI_CLOCK_DIVIDER); // you can change this clock speed

char *SSID_NAME[] = {"cnaan", "AT&T_Guest", NULL};
char *SSID_PASS[] = {"havazelet102matan45858", "Wlan4at&tguest", NULL};

// Security can be WLAN_SEC_UNSEC, WLAN_SEC_WEP, WLAN_SEC_WPA or WLAN_SEC_WPA2
#define WLAN_SECURITY   WLAN_SEC_WPA2
#define LISTEN_PORT           89    
/****************************************************/

#define PIN_CONNECTED_LED     A3
#define PIN_PROGRESS_LED      A2
#define PIN_CAR_FWD           A4
#define PIN_CAR_BWD           A5
#define PIN_CAR_SPEED         6
//A3
#define PIN_CAR_WHEEL1        A0
#define PIN_CAR_WHEEL2        A1

#define MAX_ANALOG_VALUE        1024
#define SPEED_ANALOG_MIN_VALUE  760
#define SPEED_NUM_STEPS         10
#define SPEED_MULTIPLIER        (int)((MAX_ANALOG_VALUE - SPEED_ANALOG_MIN_VALUE) / SPEED_NUM_STEPS)

/****************************************************/

Adafruit_CC3000_Server carServer(LISTEN_PORT);
#define MAX_COMMAND           1
#define MAX_VALUE             4
#define BUFFER_SIZE           MAX_COMMAND + 1 + MAX_VALUE + 1
char mBuffer[BUFFER_SIZE+1];
char mCommand[MAX_COMMAND+1];
char mValue[MAX_VALUE+1];
int mBufindex = 0;

#define TIMEOUT_MS            500
#define DHCP_TIMEOUT          8000

/****************************************************/

/////////////////////// SETUP
void setup(void)
{
  Serial.begin(115200);
  initPins();
  setProgressLed(TRUE);
  showConnected(TRUE);

  /* Initialise the module */
  Serial.println(F("Initializing Wi-Fi..."));
  if (!cc3000.begin())
  {
    showError();
    Serial.println(F("Couldn't begin()! Check your wiring?"));
    while(1);
  }

  Serial.println(F("Looking for known access points..."));
  uint8_t ssidIndex = selectAccessPoint();
  if (ssidIndex == -1) {
    showError();
    Serial.println(F("Known access points not found!"));
    while(1);
  }

  showConnected(FALSE);
  delay(300);
  showConnected(TRUE);
  Serial.println(F("Attempting to connect...(takes time)")); 
  if (!cc3000.connectToAP(SSID_NAME[ssidIndex], SSID_PASS[ssidIndex], WLAN_SECURITY)) {
    showError();
    Serial.println(F("Could not connect to access point!"));
    while(1);
  }
   
  Serial.println(F("Connected to access point."));  
  Serial.println(F("Requesting IP from DHCP"));
  unsigned long endtime = millis() + DHCP_TIMEOUT;
  while ((millis() < endtime) & !cc3000.checkDHCP())
  {
    delay(100); 
  }  

  /* Display the IP address DNS, Gateway, etc. */  
  int numTries = 10;
  while (numTries > 0 && ! displayConnectionDetails()) {
    numTries--;
    showConnected(FALSE);
    delay(1000);
    showConnected(TRUE);
  }
  if (numTries == 0) {
    showError();
    Serial.println(F("Could not get IP address!"));
    while(1);
  }

  // Start listening for connections
  carServer.begin();  
  Serial.println(F("Waiting for controller connection..."));
  setProgressLed(FALSE);
  showConnected(TRUE);
}

/////////////////////// LOOP
void loop(void)
{
  // Try to get a client which is connected.
  Adafruit_CC3000_ClientRef client = carServer.available();
  if (client) {
     // Check if there is data available to read.
     if (client.available() > 0) {
        showConnected(FALSE);

        // Clear the incoming data buffer and point to the beginning of it.
        mBufindex = 0;
        memset(&mBuffer, 0, sizeof(mBuffer));
        memset(&mCommand, 0, sizeof(mCommand));
        memset(&mValue, 0, sizeof(mValue));

        // Set a timeout for reading all the incoming data.
        unsigned long endtime = millis() + TIMEOUT_MS;
        // Read all the incoming data or the timeout expires.
        while ((millis() < endtime) && (mBufindex < BUFFER_SIZE)) {
          if (client.available()) {
            char ch = client.read();
            if (ch != '\n' && ch != '\r')
              mBuffer[mBufindex++] = ch;
            else
              break;
          }
        }     
        if (parseCommand(mBuffer, mBufindex, mCommand, mValue)) {
          int value = atoi(mValue);
          Serial.print(mCommand);
          Serial.print(" ");
          Serial.println(value);
          client.fastrprintln("OK");
          handleCommand(mCommand, value);
        }
        else
          Serial.println(F("Error parsing command"));
        showConnected(TRUE);
     }
  }
}

/////////////////////// SERVER AND COMMUNICATIONS
bool parseCommand(char* buf,int bufSize, char* cmd, char *value) {
    if (bufSize < 2)
      return false;
    // Parse first word up to whitespace as action.
    char* space = strtok((char*)buf, " ");
    if (space != NULL)
      strncpy(cmd, space, MAX_COMMAND);
    char* val = strtok(NULL, " ");
    if (val != NULL)
      strncpy(value, val, MAX_VALUE);
    return true;
}

bool displayConnectionDetails(void)
{
  uint32_t ipAddress, netmask, gateway, dhcpserv, dnsserv;
  
  if(!cc3000.getIPAddress(&ipAddress, &netmask, &gateway, &dhcpserv, &dnsserv))
  {
    Serial.println(F("Unable to retrieve the IP Address! Retrying..."));
    return false;
  }
  else
  {
    Serial.print(F("Car IP Addr: ")); cc3000.printIPdotsRev(ipAddress);
    /*Serial.print(F("\nNetmask: ")); cc3000.printIPdotsRev(netmask);
    Serial.print(F("\nGateway: ")); cc3000.printIPdotsRev(gateway);
    Serial.print(F("\nDHCPsrv: ")); cc3000.printIPdotsRev(dhcpserv);
    Serial.print(F("\nDNSserv: ")); cc3000.printIPdotsRev(dnsserv);*/
    Serial.println();
    return true;
  }
}

uint32_t selectAccessPoint() 
{
  uint32_t index;
  uint8_t valid, rssi, sec;
  char ssidname[33]; 
  uint32_t found_index = 0;
  int names = 0;

  if (!cc3000.startSSIDscan(&index)) {
    Serial.println(F("SSID scan failed!"));
    return -1;
  }

  while (index) {
    index--;
    names = 0;
    valid = cc3000.getNextSSID(&rssi, &sec, ssidname);
    while (SSID_NAME[names] != NULL) {
      if (strcmp(ssidname,SSID_NAME[names]) == 0) {
        Serial.print(F("SSID "));Serial.print(SSID_NAME[names]);Serial.println(F(" Found"));      
        cc3000.stopSSIDscan();
        return names;
      }
      names++;
    }
  }
  cc3000.stopSSIDscan();
  return -1;
}


void handleCommand(char *command, int value) {
  switch (command[0]) {
    case 'S':
      wheelStraight(value);
      break;
    case 'L':
      wheelLeft(value);
      break;
    case 'R':
      wheelRight(value);
      break;
    case 'P':
      power(value);
      break;
    default:
      break;
  }
}

/////////////////////// CAR CONTROL
void wheelStraight(int value) {
  analogWrite(PIN_CAR_WHEEL1, LOW);
  analogWrite(PIN_CAR_WHEEL2, LOW);        
}

void wheelLeft(int value) {
  analogWrite(PIN_CAR_WHEEL1, MAX_ANALOG_VALUE/2);
  analogWrite(PIN_CAR_WHEEL2, LOW);        
}

void wheelRight(int value) {
  analogWrite(PIN_CAR_WHEEL1, LOW);
  analogWrite(PIN_CAR_WHEEL2, MAX_ANALOG_VALUE/2);        
}

void power(int value) {
  if (value > 0) {
    analogWrite(PIN_CAR_FWD, MAX_ANALOG_VALUE);
    analogWrite(PIN_CAR_BWD, LOW);
  }
  else if (value < 0) {
    analogWrite(PIN_CAR_FWD, LOW);
    analogWrite(PIN_CAR_BWD, MAX_ANALOG_VALUE);    
  }
  else {
    analogWrite(PIN_CAR_FWD, LOW);
    analogWrite(PIN_CAR_BWD, LOW);        
  }
  int speed = getSpeed(value);
  Serial.println("Speed : ");Serial.println(speed);
  analogWrite (PIN_CAR_SPEED, speed);
}

int getSpeed(int value) {
  if (value == 1)
    return 0;
  if (value < 0)
    value = -value;
  return SPEED_ANALOG_MIN_VALUE + (int)(value * SPEED_MULTIPLIER);
}

/////////////////////// PINS
void initPins() {
  pinMode(PIN_CONNECTED_LED, OUTPUT);
  analogWrite(PIN_CONNECTED_LED, LOW);
  pinMode(PIN_CAR_FWD, OUTPUT);
  analogWrite(PIN_CAR_FWD, LOW);
  pinMode(PIN_CAR_BWD, OUTPUT);
  analogWrite(PIN_CAR_BWD, LOW);
  pinMode(PIN_CAR_SPEED, OUTPUT);
  analogWrite(PIN_CAR_SPEED, LOW);
  pinMode(PIN_CAR_WHEEL1, OUTPUT);
  analogWrite(PIN_CAR_WHEEL1, LOW);
  pinMode(PIN_CAR_WHEEL2, OUTPUT);
  analogWrite(PIN_CAR_WHEEL2, LOW);
}

/////////////////////// LEDS
void showConnected(bool on) {
  if (on)
    analogWrite(PIN_CONNECTED_LED, MAX_ANALOG_VALUE);
  else
    analogWrite(PIN_CONNECTED_LED, LOW);
}

void showError() {
  digitalWrite(PIN_CONNECTED_LED, LOW);
  analogWrite(PIN_PROGRESS_LED, MAX_ANALOG_VALUE);
}

void setProgressLed(bool on) {
  if (on)
    analogWrite(PIN_PROGRESS_LED, MAX_ANALOG_VALUE);
  else
    analogWrite(PIN_PROGRESS_LED, LOW);
}
